# Fritzing sketch 10WLEDbulb-reed_ON (saved by Fritzing 0.9.3b)
breadboards: 1

parts:
  5V_2A_or_12V_1_5A_(or_higher) = Power plug
  Reed = SWITCH-MOMENTARY-2 [package=reed_switch_pth]
  resistor = Resistor [tolerance=±5% resistance=10k package="0805 [SMD]"]
  resistor_2 = Resistor [tolerance=±5% resistance=100 package="0805 [SMD]"]
  LED_bulb_5-12V;_10W(max) = LEDs [package=led10mm]
  IRLZ44N = Basic FET N-Channel [package="DPak [SMD]"]

nets:
  N1: 5V_2A_or_12V_1_5A_(or_higher).GND, resistor.Pin_1, IRLZ44N.source
  N2: 5V_2A_or_12V_1_5A_(or_higher).VCC, Reed.1, LED_bulb_5-12V;_10W(max).C
  N3: Reed.2, resistor_2.Pin_0
  N4: resistor.Pin_0, resistor_2.Pin_1, IRLZ44N.Gate
  N5: LED_bulb_5-12V;_10W(max).A, IRLZ44N.drain

notes:
  LIGHT ON
  Turn on an LED bulb when a magnet approaches the reed switch
  * not suitable for bare COB lights

custom parts:
  LEDs: LEDs Standard schematic elements and footprints for 5mm, 3mm, 1206, and 0603 sized LEDs. 5mm - Spark Fun Electronics SKU : COM-00529 (and others)
