# Fritzing sketch 2pin-Reed_ON (saved by Fritzing 0.9.3b)
breadboards: 1

parts:
  Reed = Reed switch [package=THT]
  Resistor = Resistor [tolerance=±5% resistance=220 package="2010 [SMD]"]
  LED_(20mA_only) = smd LED [color="Red (633nm)" package="1206 [SMD]"]
  Power_plug1 = Power plug

nets:
  N1: Reed.pin_1, Resistor.Pin_1
  N2: Reed.pin_2, Power_plug1.VCC
  N3: Resistor.Pin_0, LED_(20mA_only).anode
  N4: LED_(20mA_only).cathode, Power_plug1.GND

notes:
  LED ON
  Turn on and LED when approaching a magnet to the reed sensor
  Power → resistor value
  5 V → 220 Ω
  9 V → 470 Ω
  12 V → 1 kΩ
